// Logisim project Project2Given.circ as structural Verilog: 4 circuits, main circuit main
module main (
);

  wire and_1_out, and_2_out, B0, B1, B2, B3, B4, B5, B6, B7, B8, B9, BL, BU, C0, C1, C2, CLK, L1_l, L1_u,
       not_1_out, or_8_out, P1_v, R0, R1, R3, R4, Valid;
  wire [2:0] counter_1_q;
  wire [3:0] IB1_c0, P1_b0, register_2_q, register_3_q, register_4_q, register_5_q;

  Button n1 (.out(B1));
  Button n4 (.out(B4));
  Button n7 (.out(B7));
  Button L (.out(BL));
  Button n3 (.out(B3));
  Button n2 (.out(B2));
  Button n6 (.out(B6));
  Button n5 (.out(B5));
  Button n9 (.out(B9));
  Button n8 (.out(B8));
  Button U (.out(BU));
  Button n0 (.out(B0));
  or or_1 (R0, B3, B2, B1);
  or or_2 (R1, B6, B5, B4);
  or or_3 (R3, B9, B8, B7);
  or or_4 (R4, BU, B0, BL);
  or or_5 (C0, B1, B4, B7, BL);
  or or_6 (C1, B2, B5, B8, B0);
  or or_7 (C2, B3, B6, B9, BU);
  Clock clock_1 (.out(CLK));
  nand nand_1 (Valid, IB1_c0[0], IB1_c0[1], IB1_c0[2], IB1_c0[3]);
  // Probe on P1_b0
  Panel P1 (
    .R0(R0), .R1(R1), .R2(R3), .R3(R4), .C0(C0), .C1(C1), .C2(C2), .B0(P1_b0[0]), .B1(P1_b0[1]),
    .B2(P1_b0[2]), .B3(P1_b0[3]), .V(P1_v));
  LED Press (.in(P1_v));
  // Probe on IB1_c0
  InputBuffer IB1 (
    .B0(P1_b0[0]), .B1(P1_b0[1]), .B2(P1_b0[2]), .B3(P1_b0[3]), .V(P1_v), .CLK(not_1_out), .C0(IB1_c0[0]),
    .C1(IB1_c0[1]), .C2(IB1_c0[2]), .C3(IB1_c0[3]));
  not not_1 (not_1_out, CLK);
  Register #(.width(4)) register_1 (.D(register_2_q), .en(Valid), .clk(CLK));  // open: Q, clr
  Lock L1 (.C0(IB1_c0[0]), .C1(IB1_c0[1]), .C2(IB1_c0[2]), .C3(IB1_c0[3]), .CLK(CLK), .L(L1_l), .U(L1_u));
  Counter #(.max('h7), .width(3)) counter_1 (
    .count(or_8_out), .Q(counter_1_q), .up(L1_u), .clk(CLK));  // open: load, D, carry, clr
  or or_8 (or_8_out, L1_l, L1_u);
  Register #(.width(4)) register_2 (.D(register_3_q), .en(Valid), .clk(CLK), .Q(register_2_q));  // open: clr
  LED Unlocked (.in(and_1_out));
  and and_1 (and_1_out, ~counter_1_q[0], ~counter_1_q[1], ~counter_1_q[2]);  // AND_Gate
  Register #(.width(4)) register_3 (.D(register_4_q), .en(Valid), .clk(CLK), .Q(register_3_q));  // open: clr
  LED Locked (.in(and_2_out));
  and and_2 (and_2_out, ~counter_1_q[0], ~counter_1_q[1], counter_1_q[2]);  // AND_Gate
  Register #(.width(4)) register_4 (.D(register_5_q), .en(Valid), .clk(CLK), .Q(register_4_q));  // open: clr
  Register #(.width(4)) register_5 (.D(IB1_c0), .en(Valid), .clk(CLK), .Q(register_5_q));  // open: clr
endmodule

module Panel (
  input  R0,
  input  R1,
  input  R2,
  input  R3,
  input  C0,
  input  C1,
  input  C2,
  output B0,
  output B1,
  output B2,
  output B3,
  output V
);

  wire CA_out, cm1_out, cm2_out, cm3_out, CM_out, K0, K1, K2, K3, K4, K5, K6, K7, K8, K9, KL, KU, not_1_out,
       not_2_out, RA_out, rm1_out, rm2_out, rm3_out, rm4_out, rm5_out, rm6_out, RM_out, VC_out, VR_out;

  and u_K1 (K1, R0, C0);
  and u_K2 (K2, R0, C1);
  and u_K3 (K3, R0, C1);
  and u_K4 (K4, R1, C0);
  and u_K5 (K5, R1, C1);
  and u_K6 (K6, R1, C2);
  and u_K7 (K7, R2, C0);
  and u_K8 (K8, R2, C1);
  and u_K9 (K9, R2, C2);
  and u_KL (KL, R3, C0);
  and u_K0 (K0, R3, C1);
  and u_KU (KU, R3, C2);
  or RA (RA_out, R0, R1, R2, R3);
  and rm1 (rm1_out, R0, R1);
  and rm2 (rm2_out, R0, R2);
  and rm3 (rm3_out, R0, R3);
  and rm4 (rm4_out, R1, R2);
  and rm5 (rm5_out, R1, R3);
  and rm6 (rm6_out, R2, R3);
  and cm1 (cm1_out, C0, C1);
  and cm2 (cm2_out, C0, C2);
  and cm3 (cm3_out, C1, C2);
  or RM (RM_out, rm1_out, rm2_out, rm3_out, rm4_out, rm5_out, rm6_out);
  not not_1 (not_1_out, RM_out);
  or CM (CM_out, cm1_out, cm2_out, cm3_out);
  not not_2 (not_2_out, CM_out);
  or CA (CA_out, C0, C1, C2);
  and VR (VR_out, RA_out, not_1_out);
  and VC (VC_out, CA_out, not_2_out);
  or B00 (B0, K1, K3, K5, K7, K9, KU);
  or B01 (B1, K2, K3, K6, K7, KL, KU);
  or B02 (B2, K4, K5, K6, K7);
  or B03 (B3, K8, K9, KL, KU);
  and and_1 (V, VR_out, VC_out);
endmodule

module InputBuffer (
  input  B0,
  input  B1,
  input  B2,
  input  B3,
  input  V,
  input  CLK,
  output C0,
  output C1,
  output C2,
  output C3
);

  wire Enable_out, iE_out, iW_out, ns0_out, ns1_out, T1_out, T2_out;
  wire [1:0] N0_out, State_q;
  wire [3:0] code_q;

  Register #(.width(4)) code (.D({B3, B2, B1, B0}), .en(Enable_out), .clk(CLK), .Q(code_q));  // open: clr
  Register #(.width(2)) State (.D(N0_out), .en(1'b1), .clk(CLK), .Q(State_q));  // open: clr
  not ns0 (ns0_out, State_q[0]);
  not ns1 (ns1_out, State_q[1]);
  Lock lock_1 (.L(State_q[0]), .U(State_q[0]));  // open: C0, C1, C2, C3, CLK
  and iW (iW_out, ns0_out, ns1_out);
  and iE (iE_out, ns1_out, State_q[0]);
  and T1 (T1_out, ns1_out, State_q[0]);
  and T2 (T2_out, State_q[1], ns0_out, V);
  and Enable (Enable_out, V, iW_out);
  or N1 (N0_out[1], T1_out, T2_out);
  and N0 (N0_out[0], ns0_out, ns1_out, V);
  Multiplexer #(.width(4)) multiplexer_1 (.in0(4'b1111), .in1(code_q), .out({C3, C2, C1, C0}), .sel(iE_out));
endmodule

module Lock (
  input  C0,
  input  C1,
  input  C2,
  input  C3,
  input  CLK,
  output L,
  output U
);

  wire eqF_out, eqL_out, eqU_out, hasDigit, k0, k0_n, k1, k1_n, Locked_out, neqL, neqU, not_1_out, not_2_out,
       not_3_out, not_4_out, not_7_out, not_8_out, not_11_out, not_12_out, nt0, nt1, p0, p1, ph00, ph01,
       ph10, ph11, Spin, t0, t1, Unlocked_out, WE_UC1_out, WE_UC2_out, WE_UC3_out;

  not not_1 (not_1_out, C0);
  not not_2 (not_2_out, C1);
  not not_3 (not_3_out, C2);
  not not_4 (not_4_out, C3);
  and eqL (eqL_out, C3, not_3_out, C1, not_1_out);
  and eqU (eqU_out, C3, not_3_out, C1, C0);
  and eqF (eqF_out, C0, C1, C2, C3);
  not not_5 (hasDigit, eqF_out);
  Register #(.width(4)) UC1 (.D({C3, C2, C1, C0}), .en(WE_UC1_out), .clk(CLK), .clr(1'b0));  // open: Q
  Register #(.width(4)) UC2 (.D({C3, C2, C1, C0}), .en(WE_UC2_out), .clk(CLK), .clr(1'b0));  // open: Q
  Register #(.width(4)) UC3 (.D({C3, C2, C1, C0}), .en(WE_UC3_out), .clk(CLK), .clr(1'b0));  // open: Q
  Register #(.width(2)) K (.en(1'b1), .clk(CLK), .Q({k1, k0}), .clr(1'b0));  // open: D
  not not_6 (k0_n, k0);
  nor nor_1 (k1_n, k0, k1);
  // AND_Gate kD has open pins: in0=k0, in1=k1, out=open
  Register #(.width(2)) register_1 (.en(1'b1), .clk(CLK), .Q({p1, p0}), .clr(1'b0));  // open: D
  Register #(.width(2)) TOP (.en(1'b1), .clk(CLK), .Q({t1, t0}), .clr(1'b0));  // open: D
  Multiplexer multiplexer_1 (.in0(1'b0), .in1(k0_n), .sel(Spin));  // open: out
  Multiplexer multiplexer_2 (.in0(1'b0), .in1(k1_n), .sel(Spin));  // open: out
  not not_7 (not_7_out, p0);
  not not_8 (not_8_out, p1);
  not not_9 (neqL, eqL_out);
  not not_10 (neqU, eqU_out);
  and and_1 (ph00, not_8_out, not_7_out);
  and and_2 (ph01, not_8_out, p0);
  and and_3 (ph10, p1, not_7_out);
  and and_4 (ph11, p1, p0);
  not not_11 (not_11_out, neqL);
  not not_12 (not_12_out, neqU);
  and WE_UC1 (WE_UC1_out, Unlocked_out, ph01, hasDigit, neqL, neqU);
  and WE_UC2 (WE_UC2_out, Unlocked_out, ph10, hasDigit, neqL, neqU);
  and WE_UC3 (WE_UC3_out, Unlocked_out, ph11, hasDigit, neqL, neqU);
  // AND_Gate u_start has open pins: in0=Unlocked_out, in1=ph00, in2=hasDigit, in3=not_11_out, out=open
  // AND_Gate u_doubleL has open pins: in0=Unlocked_out, in1=ph01, in2=hasDigit, in3=not_11_out, out=open
  // AND_Gate u_cancel01 has open pins: in0=Unlocked_out, in1=ph01, in2=hasDigit, in3=not_12_out, out=open
  // AND_Gate u_restart10 has open pins: in0=Unlocked_out, in1=ph10, in2=hasDigit, in3=not_11_out, out=open
  // AND_Gate u_cancel10 has open pins: in0=Unlocked_out, in1=ph10, in2=hasDigit, in3=not_12_out, out=open
  // AND_Gate u_restart11 has open pins: in0=Unlocked_out, in1=ph11, in2=hasDigit, in3=not_11_out, out=open
  // AND_Gate u_cancel11 has open pins: in0=Unlocked_out, in1=ph11, in2=hasDigit, in3=not_12_out, out=open
  not not_13 (nt0, t0);
  not not_14 (nt1, t1);
  and Unlocked (Unlocked_out, nt0, nt1);
  and Locking (L, nt1, t0);
  and Locked (Locked_out, t1, nt0);
  and Unlocking (U, t0, t1);
  or or_1 (Spin, Unlocked_out, Locked_out);
endmodule
