// Logisim project Project2GivenFinal.circ as structural Verilog: 4 circuits, main circuit main
module main (
);

  wire and_1_out, and_2_out, B0, B1, B2, B3, B4, B5, B6, B7, B8, B9, BL, BU, C0, C1, C2, CLK, L1_l, L1_u,
       not_1_out, or_8_out, P1_v, R0, R1, R3, R4, Valid;
  wire [2:0] counter_1_q;
  wire [3:0] IB1_c0, P1_b0, register_2_q, register_3_q, register_4_q, register_5_q;

  Button n1 (.out(B1));
  Button n4 (.out(B4));
  Button n7 (.out(B7));
  Button L (.out(BL));
  Button n3 (.out(B3));
  Button n2 (.out(B2));
  Button n6 (.out(B6));
  Button n5 (.out(B5));
  Button n9 (.out(B9));
  Button n8 (.out(B8));
  Button U (.out(BU));
  Button n0 (.out(B0));
  or or_1 (R0, B3, B2, B1);
  or or_2 (R1, B6, B5, B4);
  or or_3 (R3, B9, B8, B7);
  or or_4 (R4, BU, B0, BL);
  or or_5 (C0, B1, B4, B7, BL);
  or or_6 (C1, B2, B5, B8, B0);
  or or_7 (C2, B3, B6, B9, BU);
  Clock clock_1 (.out(CLK));
  nand nand_1 (Valid, IB1_c0[0], IB1_c0[1], IB1_c0[2], IB1_c0[3]);
  // Probe on P1_b0
  Panel P1 (
    .R0(R0), .R1(R1), .R2(R3), .R3(R4), .C0(C0), .C1(C1), .C2(C2), .B0(P1_b0[0]), .B1(P1_b0[1]),
    .B2(P1_b0[2]), .B3(P1_b0[3]), .V(P1_v));
  LED Press (.in(P1_v));
  // Probe on IB1_c0
  InputBuffer IB1 (
    .B0(P1_b0[0]), .B1(P1_b0[1]), .B2(P1_b0[2]), .B3(P1_b0[3]), .V(P1_v), .CLK(not_1_out), .C0(IB1_c0[0]),
    .C1(IB1_c0[1]), .C2(IB1_c0[2]), .C3(IB1_c0[3]));
  not not_1 (not_1_out, CLK);
  Register #(.width(4)) register_1 (.D(register_2_q), .en(Valid), .clk(CLK));  // open: Q, clr
  Lock L1 (.C0(IB1_c0[0]), .C1(IB1_c0[1]), .C2(IB1_c0[2]), .C3(IB1_c0[3]), .CLK(CLK), .L(L1_l), .U(L1_u));
  Counter #(.max('h7), .width(3)) counter_1 (
    .count(or_8_out), .Q(counter_1_q), .up(L1_u), .clk(CLK));  // open: load, D, carry, clr
  or or_8 (or_8_out, L1_l, L1_u);
  Register #(.width(4)) register_2 (.D(register_3_q), .en(Valid), .clk(CLK), .Q(register_2_q));  // open: clr
  LED Unlocked (.in(and_1_out));
  and and_1 (and_1_out, ~counter_1_q[0], ~counter_1_q[1], ~counter_1_q[2]);  // AND_Gate
  Register #(.width(4)) register_3 (.D(register_4_q), .en(Valid), .clk(CLK), .Q(register_3_q));  // open: clr
  LED Locked (.in(and_2_out));
  and and_2 (and_2_out, ~counter_1_q[0], ~counter_1_q[1], counter_1_q[2]);  // AND_Gate
  Register #(.width(4)) register_4 (.D(register_5_q), .en(Valid), .clk(CLK), .Q(register_4_q));  // open: clr
  Register #(.width(4)) register_5 (.D(IB1_c0), .en(Valid), .clk(CLK), .Q(register_5_q));  // open: clr
endmodule

module Panel (
  input  R0,
  input  R1,
  input  R2,
  input  R3,
  input  C0,
  input  C1,
  input  C2,
  output B0,
  output B1,
  output B2,
  output B3,
  output V
);

  wire CA_out, cm1_out, cm2_out, cm3_out, CM_out, K0, K1, K2, K3, K4, K5, K6, K7, K8, K9, KL, KU, not_1_out,
       not_2_out, RA_out, rm1_out, rm2_out, rm3_out, rm4_out, rm5_out, rm6_out, RM_out, VC_out, VR_out;

  and u_K1 (K1, R0, C0);
  and u_K2 (K2, R0, C1);
  and u_K3 (K3, R0, C1);
  and u_K4 (K4, R1, C0);
  and u_K5 (K5, R1, C1);
  and u_K6 (K6, R1, C2);
  and u_K7 (K7, R2, C0);
  and u_K8 (K8, R2, C1);
  and u_K9 (K9, R2, C2);
  and u_KL (KL, R3, C0);
  and u_K0 (K0, R3, C1);
  and u_KU (KU, R3, C2);
  or RA (RA_out, R0, R1, R2, R3);
  and rm1 (rm1_out, R0, R1);
  and rm2 (rm2_out, R0, R2);
  and rm3 (rm3_out, R0, R3);
  and rm4 (rm4_out, R1, R2);
  and rm5 (rm5_out, R1, R3);
  and rm6 (rm6_out, R2, R3);
  and cm1 (cm1_out, C0, C1);
  and cm2 (cm2_out, C0, C2);
  and cm3 (cm3_out, C1, C2);
  or RM (RM_out, rm1_out, rm2_out, rm3_out, rm4_out, rm5_out, rm6_out);
  not not_1 (not_1_out, RM_out);
  or CM (CM_out, cm1_out, cm2_out, cm3_out);
  not not_2 (not_2_out, CM_out);
  or CA (CA_out, C0, C1, C2);
  and VR (VR_out, RA_out, not_1_out);
  and VC (VC_out, CA_out, not_2_out);
  or B00 (B0, K1, K3, K5, K7, K9, KU);
  or B01 (B1, K2, K3, K6, K7, KL, KU);
  or B02 (B2, K4, K5, K6, K7);
  or B03 (B3, K8, K9, KL, KU);
  and and_1 (V, VR_out, VC_out);
endmodule

module InputBuffer (
  input  B0,
  input  B1,
  input  B2,
  input  B3,
  input  V,
  input  CLK,
  output C0,
  output C1,
  output C2,
  output C3
);

  wire Enable_out, iE_out, iW_out, ns0_out, ns1_out, T1_out, T2_out;
  wire [1:0] N0_out, State_q;
  wire [3:0] code_q;

  Register #(.width(4)) code (.D({B3, B2, B1, B0}), .en(Enable_out), .clk(CLK), .Q(code_q));  // open: clr
  Register #(.width(2)) State (.D(N0_out), .en(1'b1), .clk(CLK), .Q(State_q));  // open: clr
  not ns0 (ns0_out, State_q[0]);
  not ns1 (ns1_out, State_q[1]);
  Lock lock_1 (.L(State_q[0]), .U(State_q[0]));  // open: C0, C1, C2, C3, CLK
  and iW (iW_out, ns0_out, ns1_out);
  and iE (iE_out, ns1_out, State_q[0]);
  and T1 (T1_out, ns1_out, State_q[0]);
  and T2 (T2_out, State_q[1], ns0_out, V);
  and Enable (Enable_out, V, iW_out);
  or N1 (N0_out[1], T1_out, T2_out);
  and N0 (N0_out[0], ns0_out, ns1_out, V);
  Multiplexer #(.width(4)) multiplexer_1 (.in0(4'b1111), .in1(code_q), .out({C3, C2, C1, C0}), .sel(iE_out));
endmodule

module Lock (
  input  C0,
  input  C1,
  input  C2,
  input  C3,
  input  CLK,
  output L,
  output U
);

  wire A, B, b10_out, b11_out, b12_out, b13_out, b20_out, b21_out, b22_out, b23_out, b30_out, b31_out,
       b32_out, b33_out, C, D, E, enterlocking_out, enterspin_out, eqF_out, eqL_out, eqU_out, eqUC1_out,
       eqUC2_out, eqUC3_out, F, Forc_out, FORCED_LSB_out, Forced_LSBit_out, FORCED_MSB_out, Forced_MSBit_out,
       Forced_out, hasDigit, k0, k0_n, k1, k1_n, kDone_out, Locked_out, m1_out, m2_out, m3_out, mismatch_out,
       neqL, neqU, not_1_out, not_2_out, not_3_out, not_4_out, not_6_out, not_7_out, not_10_out, not_11_out,
       not_12_out, not_13_out, not_14_out, not_15_out, not_16_out, not_17_out, not_18_out, not_19_out,
       not_20_out, not_21_out, not_22_out, not_23_out, nt0, nt1, p0, p1, P_a_t, P_B_out, P_C_out, P_D_out,
       P_E_out, P_F_out, Pb_out, Pc_out, Pd_out, Pe_out, ph00, ph01, ph10, ph11, PHL0_Next, PHL1_Next,
       PHU0_next, PHU1_next, Spin, t0, t1, u_cancel01_out, u_cancel10_out, u_cancel11_out, u_doubleL_out,
       u_restart10_out, u_restart11_out, Unlocked_out, v1ok_out, v2ok_out, v3ok_out, verify_window_out,
       WE_UC3_out;
  wire [1:0] PH_D, PH_nest_sel;
  wire [3:0] UC1_q, UC2_q, UC3_q;

  not not_1 (not_1_out, C0);
  not not_2 (not_2_out, C1);
  not not_3 (not_3_out, C2);
  not not_4 (not_4_out, C3);
  and eqL (eqL_out, C3, not_3_out, C1, not_1_out);
  and eqU (eqU_out, C3, not_3_out, C1, C0);
  and eqF (eqF_out, C0, C1, C2, C3);
  not not_5 (hasDigit, eqF_out);
  Register #(.width(4)) UC1 (.D({C3, C2, C1, C0}), .en(E), .clk(CLK), .Q(UC1_q), .clr(1'b0));
  Register #(.width(4)) UC2 (.D({C3, C2, C1, C0}), .en(D), .clk(CLK), .Q(UC2_q), .clr(1'b0));
  Register #(.width(4)) UC3 (.D({C3, C2, C1, C0}), .en(WE_UC3_out), .clk(CLK), .Q(UC3_q), .clr(1'b0));
  Register #(.width(2)) K (.D({k1_n, k0_n}), .en(1'b1), .clk(CLK), .Q({k1, k0}), .clr(1'b0));
  not k0_next (k0_n, k0);
  xor k1_next (k1_n, k0, k1);
  and kDone (kDone_out, k0, k1);
  xnor b10 (b10_out, UC1_q[0], C0);
  xnor b11 (b11_out, UC1_q[1], C1);
  xnor b12 (b12_out, UC1_q[2], C2);
  xnor b13 (b13_out, UC1_q[3], C3);
  and eqUC1 (eqUC1_out, b10_out, b11_out, b12_out, b13_out);
  xnor b30 (b30_out, UC3_q[0], C0);
  xnor b31 (b31_out, UC3_q[1], C1);
  xnor b32 (b32_out, UC3_q[2], C2);
  xnor b33 (b33_out, UC3_q[3], C3);
  xnor b20 (b20_out, UC2_q[0], C0);
  xnor b21 (b21_out, UC2_q[1], C1);
  xnor b22 (b22_out, UC2_q[2], C2);
  xnor b23 (b23_out, UC2_q[3], C3);
  and eqUC3 (eqUC3_out, b30_out, b31_out, b32_out, b33_out);
  and eqUC2 (eqUC2_out, b20_out, b21_out, b22_out, b23_out);
  Register #(.width(2)) PH (.D(PH_D), .en(1'b1), .clk(CLK), .Q({p1, p0}), .clr(1'b0));
  Register #(.width(2)) TOP (.en(1'b1), .clk(CLK), .Q({t1, t0}), .clr(1'b0));  // open: D
  Multiplexer multiplexer_1 (.in0(1'b0), .in1(k0_n), .sel(Spin));  // open: out
  Multiplexer multiplexer_2 (.in0(1'b0), .in1(k1_n), .sel(Spin));  // open: out
  not not_6 (not_6_out, p0);
  not not_7 (not_7_out, p1);
  not not_8 (neqU, eqU_out);
  not not_9 (neqL, eqL_out);
  and and_1 (ph00, not_7_out, not_6_out);
  and and_2 (ph01, not_7_out, p0);
  and and_3 (ph10, p1, not_6_out);
  and and_4 (ph11, p1, p0);
  not not_10 (not_10_out, neqU);
  not not_11 (not_11_out, neqL);
  and WE_UC1 (E, Unlocked_out, ph01, hasDigit, neqL, neqU);
  and WE_UC2 (D, Unlocked_out, ph10, hasDigit, neqL, neqU);
  and WE_UC3 (WE_UC3_out, Unlocked_out, ph11, hasDigit, neqL, neqU);
  and u_start (F, Unlocked_out, ph00, hasDigit, not_11_out);
  and u_doubleL (u_doubleL_out, Unlocked_out, ph01, hasDigit, not_11_out);
  and u_cancel01 (u_cancel01_out, Unlocked_out, ph01, hasDigit, not_10_out);
  and u_restart10 (u_restart10_out, Unlocked_out, ph10, hasDigit, not_11_out);
  and u_cancel10 (u_cancel10_out, Unlocked_out, ph10, hasDigit, not_10_out);
  and u_restart11 (u_restart11_out, Unlocked_out, ph11, hasDigit, not_11_out);
  or enterlocking (enterlocking_out, WE_UC3_out, u_doubleL_out);
  or u_A (A, WE_UC3_out, u_doubleL_out);
  or u_B (B, u_cancel11_out, u_cancel10_out, u_cancel01_out);
  or u_C (C, u_restart10_out, u_restart11_out);
  and u_cancel11 (u_cancel11_out, Unlocked_out, ph11, hasDigit, not_10_out);
  not not_12 (not_12_out, A);
  not not_13 (not_13_out, B);
  not not_14 (not_14_out, C);
  not not_15 (not_15_out, D);
  not not_16 (not_16_out, E);
  and P_B (P_B_out, not_12_out, B);
  and P_D (P_D_out, not_12_out, not_13_out, not_14_out, D);
  and P_E (P_E_out, not_12_out, not_13_out, not_14_out, not_15_out, E);
  and P_F (P_F_out, not_12_out, not_13_out, not_14_out, not_15_out, not_16_out, F);
  and P_C (P_C_out, not_12_out, not_13_out, C);
  or Forced (Forced_out, A, P_B_out, P_C_out, P_D_out, P_E_out, P_F_out);
  or Forced_MSBit (Forced_MSBit_out, P_D_out, P_E_out);
  or Forced_LSBit (Forced_LSBit_out, P_C_out, P_D_out, P_F_out);
  Multiplexer multiplexer_3 (.in0(p0), .in1(Forced_MSBit_out), .out(PHU1_next), .sel(Forced_out));
  Multiplexer multiplexer_4 (.in0(p1), .in1(Forced_LSBit_out), .out(PHU0_next), .sel(Forced_out));
  Multiplexer #(.width(2)) multiplexer_5 (
    .in0({PHU1_next, PHU0_next}), .in1({PHU1_next, PHU0_next}), .sel(Unlocked_out));  // open: out
  and verify_window (verify_window_out, neqU, neqL, hasDigit, Locked_out);
  not not_17 (not_17_out, eqUC1_out);
  not not_18 (not_18_out, eqUC2_out);
  and v1ok (v1ok_out, verify_window_out, ph01, eqUC1_out);
  and v2ok (v2ok_out, verify_window_out, ph10, eqUC2_out);
  and v3ok (v3ok_out, verify_window_out, ph11, eqUC3_out);
  not not_19 (not_19_out, eqUC3_out);
  and m1 (m1_out, verify_window_out, ph01, not_17_out);
  and m2 (m2_out, verify_window_out, ph10, not_18_out);
  and m3 (m3_out, verify_window_out, ph11, not_19_out);
  or enterspin (enterspin_out, v3ok_out, enterlocking_out);
  or mismatch (mismatch_out, m1_out, m2_out, m3_out);
  Multiplexer #(.width(2)) multiplexer_6 (.in0(PH_nest_sel), .in1(2'b00), .out(PH_D), .sel(enterspin_out));
  and L_start (P_a_t, Locked_out, ph00, hasDigit, not_10_out);
  not not_20 (not_20_out, P_a_t);
  not not_21 (not_21_out, v3ok_out);
  not not_22 (not_22_out, v2ok_out);
  not not_23 (not_23_out, v1ok_out);
  and Pb (Pb_out, not_20_out, v3ok_out);
  and Pc (Pc_out, not_20_out, not_21_out, v2ok_out);
  and Pd (Pd_out, not_20_out, not_21_out, not_22_out, v1ok_out);
  and Pe (Pe_out, not_20_out, not_21_out, not_22_out, not_23_out, mismatch_out);
  or FORCED_MSB (FORCED_MSB_out, Pc_out, Pd_out);
  or FORCED_LSB (FORCED_LSB_out, P_a_t, Pc_out);
  or Forc (Forc_out, P_a_t, Pb_out, Pc_out, Pd_out, Pe_out);
  Multiplexer multiplexer_7 (.in0(p1), .in1(FORCED_MSB_out), .out(PHL1_Next), .sel(Forc_out));
  Multiplexer multiplexer_8 (.in0(p0), .in1(FORCED_LSB_out), .out(PHL0_Next), .sel(Forc_out));
  Multiplexer #(.width(2)) multiplexer_9 ();  // open: in0, in1, out, sel
  Multiplexer #(.width(2)) multiplexer_10 ();  // open: in0, in1, out, sel
  Multiplexer #(.width(2)) multiplexer_11 (.sel(enterlocking_out));  // open: in0, in1, out
  Multiplexer #(.width(2)) multiplexer_12 (.sel(enterlocking_out));  // open: in0, in1, out
  Multiplexer #(.width(2)) multiplexer_13 (
    .in0({PHL1_Next, PHL0_Next}), .in1({PHU1_next, PHU0_next}), .out(PH_nest_sel), .sel(Unlocked_out));
  Multiplexer #(.width(2)) multiplexer_14 ();  // open: in0, in1, out, sel
  Multiplexer #(.width(2)) multiplexer_15 ();  // open: in0, in1, out, sel
  Multiplexer #(.width(2)) multiplexer_16 (.sel(v3ok_out));  // open: in0, in1, out
  Multiplexer #(.width(2)) multiplexer_17 (.sel(v3ok_out));  // open: in0, in1, out
  not not_24 (nt0, t0);
  not not_25 (nt1, t1);
  and Unlocked (Unlocked_out, nt0, nt1);
  and Locking (L, nt1, t0);
  and Locked (Locked_out, t1, nt0);
  and Unlocking (U, t0, t1);
  or or_1 (Spin, L, U);

  // Other names for the same wires on the sheet: P_A = A
endmodule
